// Logisim project angles.circ as structural Verilog: 6 circuits, main circuit main
module main (
  input  _1,
  input  _2,
  input  _3,
  input  _4,
  input  [1:0] _5__water_type,
  input  _6,
  input  _7,
  input  _8,
  input  _9
);

  wire [15:0] water_angles_processor_1_water_matrix;

  Water_angles_processor water_angles_processor_1 (
    ._1(_1), ._2(_2), ._3(_3), ._4(_4), ._5__water_type(_5__water_type), ._6(_6), ._7(_7), ._8(_8), ._9(_9),
    .water_matrix(water_angles_processor_1_water_matrix));
  // Probe on water_angles_processor_1_water_matrix
  DotMatrix #(.inputtype("row"), .matrixcols(4), .matrixrows(4)) dotmatrix_1 (
    .row0(water_angles_processor_1_water_matrix[15:12]), .row1(water_angles_processor_1_water_matrix[11:8]),
    .row2(water_angles_processor_1_water_matrix[7:4]), .row3(water_angles_processor_1_water_matrix[3:0]));

  // Notes on the sheet:
  //   Water angles
  //   Pin 5: water type (shall be 1, 2, or 3)
  //   Other pins: 0 for water, 1 for land
endmodule

module Water_angles_processor (
  input  _1,
  input  _2,
  input  _3,
  input  _4,
  input  [1:0] _5__water_type,
  input  _6,
  input  _7,
  input  _8,
  input  _9,
  output [15:0] water_matrix
);

  wire water_corner_image_picker_1_corner_out__corner___edges,
       water_corner_image_picker_1_corner_out__corner_only,
       water_corner_image_picker_2_corner_out__corner___edges,
       water_corner_image_picker_2_corner_out__corner_only,
       water_corner_image_picker_3_corner_out__corner___edges,
       water_corner_image_picker_3_corner_out__corner_only,
       water_corner_image_picker_4_corner_out__corner___edges,
       water_corner_image_picker_4_corner_out__corner_only;

  Water_rows_1__4 water_rows_1_4_1 (
    .horizontal(_2), .W_edge(_4), .E_edge(_6), .W_corner(_1), .E_corner(_3), .out_row(water_matrix[15:12]));
  Water_rows_2__3 water_rows_2_3_1 (.W_edge(_4), .E_edge(_6), .out_row(water_matrix[11:8]));
  Water_rows_1__4 water_rows_1_4_2 (
    .horizontal(_8), .W_edge(_4), .E_edge(_6), .W_corner(_7), .E_corner(_9), .out_row(water_matrix[3:0]));
  Water_corner_image_picker water_corner_image_picker_1 (
    .Corner(_1), .Edge_1(_2), .Edge_2(_4),
    .corner_out__corner___edges(water_corner_image_picker_1_corner_out__corner___edges),
    .corner_out__corner_only(water_corner_image_picker_1_corner_out__corner_only));
  // Probe on _4
  Water_corner_image_picker water_corner_image_picker_2 (
    .Corner(_7), .Edge_1(_4), .Edge_2(_8),
    .corner_out__corner___edges(water_corner_image_picker_2_corner_out__corner___edges),
    .corner_out__corner_only(water_corner_image_picker_2_corner_out__corner_only));
  DotMatrix #(.inputtype("row"), .matrixcols(4), .matrixrows(4)) dotmatrix_1 (
    .row0(water_matrix[15:12]), .row1(water_matrix[11:8]), .row2(water_matrix[11:8]), .row3(water_matrix[3:0]));
  // Probe on water_corner_image_picker_1_corner_out__corner___edges
  // Probe on water_corner_image_picker_1_corner_out__corner_only
  // Probe on water_corner_image_picker_2_corner_out__corner___edges
  // Probe on water_corner_image_picker_2_corner_out__corner_only
  // Probe on _2
  // Probe on _8
  Water_corner_image_picker water_corner_image_picker_3 (
    .Corner(_3), .Edge_1(_2), .Edge_2(_6),
    .corner_out__corner___edges(water_corner_image_picker_3_corner_out__corner___edges),
    .corner_out__corner_only(water_corner_image_picker_3_corner_out__corner_only));
  // Probe on _6
  Water_corner_image_picker water_corner_image_picker_4 (
    .Corner(_9), .Edge_1(_6), .Edge_2(_8),
    .corner_out__corner___edges(water_corner_image_picker_4_corner_out__corner___edges),
    .corner_out__corner_only(water_corner_image_picker_4_corner_out__corner_only));
  // Probe on water_corner_image_picker_3_corner_out__corner___edges
  // Probe on water_corner_image_picker_3_corner_out__corner_only
  // Probe on water_corner_image_picker_4_corner_out__corner___edges
  // Probe on water_corner_image_picker_4_corner_out__corner_only

  assign water_matrix[7:4] = water_matrix[11:8];

  // Other names for the same wires on the sheet: _5[1:0] = _5__water_type; E_edge = _6; N_edge = _2; NE = _3; NW = _1;
  //   S_edge = _8; SE = _9; SW = _7; W_edge = _4; Row_4[3:0] = water_matrix[3:0]; Rows_2__3[3:0] = water_matrix[11:8];
  //   Row_1[3:0] = water_matrix[15:12]

  // Notes on the sheet:
  //   Inputs
  //   Edges
  //   Corners
  //   water matrix processor
  //   tile image picker
endmodule

// water rows 1, 4
module Water_rows_1__4 (
  input  horizontal,
  input  W_edge,
  input  E_edge,
  input  W_corner,
  input  E_corner,
  output [3:0] out_row
);

  wire NE_SE_out, NW_SW_out;

  or NW_SW (NW_SW_out, horizontal, W_edge);
  or NE_SE (NE_SE_out, horizontal, E_edge);
  assign out_row[2:1] = {{1{horizontal}}, horizontal};  // Bit_Extender bit_extender_1
  Multiplexer #(.enable("false")) multiplexer_1 (.in0(W_corner), .in1(NW_SW_out), .out(out_row[3]), .sel(NW_SW_out));
  Multiplexer #(.enable("false")) multiplexer_2 (.in0(E_corner), .in1(NE_SE_out), .out(out_row[0]), .sel(NE_SE_out));
endmodule

// water rows 3, 3
module Water_rows_2__3 (
  input  W_edge,
  input  E_edge,
  output [3:0] out_row
);


  assign out_row = {W_edge, 2'b00, E_edge};
endmodule

// water corner image picker
module Water_corner_image_picker (
  input  Corner,
  input  Edge_1,
  input  Edge_2,
  output corner_out__corner___edges,
  output corner_out__corner_only
);

  wire nor_1_out;

  Multiplexer #(.enable("false")) multiplexer_1 (
    .in0(1'b0), .in1(Corner), .out(corner_out__corner_only), .sel(nor_1_out));
  nor nor_1 (nor_1_out, Edge_1, Edge_2);
  and and_1 (corner_out__corner___edges, Edge_1, Edge_2);
endmodule

module Water_edge_image_picker (
  input  Edge,
  input  Corner_1_image_picked,
  input  Corner_2_image_picked,
  output Pick_edge_image
);

  Multiplexer #(.select(2), .enable("false")) multiplexer_1 (
    .in0(Edge), .in1(1'b1), .in2(1'b1), .in3(1'b0), .out(Pick_edge_image),
    .sel({Corner_2_image_picked, Corner_1_image_picked}));
endmodule
